// Logisim project cpu.circ as structural Verilog: 10 circuits, main circuit main
module main (
  input  reset,
  output [31:0] out_2,
  output [31:0] out_3,
  output out_4,
  output [4:0] out_5,
  output [31:0] out_6,
  output out_7,
  output [31:0] out_8,
  output [31:0] out_9
);

  wire _31Sel, ALUSrc, ALUSrcA, and_1_out, and_2_out, behlbal, Branch, clk, ExtControl, jal, jr, Jump,
       MemtoReg, or_2_out, RegDst, senodb, Zero;
  wire [3:0] ALUControl;
  wire [4:0] multiplexer_1_out, spt_1__11_15, spt_1__16_20, spt_1__21_25;
  wire [15:0] Imm;
  wire [31:0] dm_1_rd, GPR_rs, multiplexer_2_out, multiplexer_4_out, multiplexer_5_out, multiplexer_6_out,
       multiplexer_7_out, PC_4, PC_prime, SignImm, subtractor_1_out;

  Clock u_clk (.out(clk));
  PC pc_1 (.PC(PC_prime), .PC_prime(out_3), .clk(clk), .clr(reset));
  Subtractor #(.width(32)) subtractor_1 (.a(out_3), .b(32'h3000), .out(subtractor_1_out));  // open: bin, bout
  CU CU (
    .in(out_2), .RegWrite(out_4), .MemWrite(out_7), .ALUControl(ALUControl), .RegDst(RegDst),
    .MemtoReg(MemtoReg), .ALUSrc(ALUSrc), .Branch(Branch), .Jump(Jump), .ExtControl(ExtControl),
    .behlbal(behlbal), .in_1(Zero), .senodb(senodb), .ALUSrcA(ALUSrcA), .jr(jr), .jal(jal));
  ROM #(.addrWidth(12), .dataWidth(32)) rom_1 (.addr(subtractor_1_out[13:2]), .data(out_2));  // open: sel
  NXTAD nxtad_1 (
    .PC_prime(PC_prime), .PC(out_3), .Zero(Zero), .Branch(Branch), .Jump(Jump), .Instr(out_2), .Imm(Imm),
    .PC_4(PC_4), .jr(jr), .GPR_rs(GPR_rs));
  SPT spt_1 (.in(out_2), ._0_15(Imm), ._16_20(spt_1__16_20), ._21_25(spt_1__21_25), ._11_15(spt_1__11_15));
  and and_1 (and_1_out, behlbal, Zero);
  GRF grf_1 (
    .RD2(out_9), .WD3(out_6), .RD1(GPR_rs), .WE3(out_4), .rst(reset), .clk(clk), .A1(spt_1__21_25),
    .A3(out_5), .A2(spt_1__16_20));
  EXT ext_1 (._15_0(Imm), .SignImm(SignImm), .ExtControl(ExtControl));
  or or_1 (_31Sel, and_1_out, jal);
  Multiplexer #(.width(5), .enable("false")) multiplexer_1 (
    .in0(spt_1__16_20), .in1(spt_1__11_15), .out(multiplexer_1_out), .sel(RegDst));
  Multiplexer #(.width(32), .enable("false")) multiplexer_2 (
    .in0(out_9), .in1(SignImm), .out(multiplexer_2_out), .sel(ALUSrc));
  Multiplexer #(.width(5), .enable("false")) multiplexer_3 (
    .in0(multiplexer_1_out), .in1({5{1'b1}}), .out(out_5), .sel(_31Sel));
  Multiplexer #(.width(32), .enable("false")) multiplexer_4 (
    .in0(GPR_rs), .in1(SignImm), .out(multiplexer_4_out), .sel(ALUSrcA));
  ALU alu_1 (
    .SrcA(multiplexer_4_out), .SrcB(multiplexer_2_out), .ALUResult(out_8), .ALUControl(ALUControl),
    .Zero(Zero));
  DM dm_1 (.A(out_8), .WD(out_9), .RD(dm_1_rd), .clk(clk), .WE(out_7), .clr(reset));
  Multiplexer #(.width(32), .enable("false")) multiplexer_5 (
    .in0(out_8), .in1(dm_1_rd), .out(multiplexer_5_out), .sel(MemtoReg));
  and and_2 (and_2_out, behlbal, Zero);
  or or_2 (or_2_out, and_2_out, jal);
  Multiplexer #(.width(32), .enable("false")) multiplexer_6 (
    .in0(multiplexer_5_out), .in1(PC_4), .out(multiplexer_6_out), .sel(or_2_out));
  Multiplexer #(.width(32), .enable("false")) multiplexer_7 (
    .in0({32{1'b0}}), .in1(32'h1), .out(multiplexer_7_out), .sel(Zero));
  Multiplexer #(.width(32), .enable("false")) multiplexer_8 (
    .in0(multiplexer_6_out), .in1(multiplexer_7_out), .out(out_6), .sel(senodb));

  // Other names for the same wires on the sheet: Instr[31:0] = out_2; MemAddr[31:0] = out_8; MemData[31:0] = out_9;
  //   MemWrite = out_7; PC[31:0] = out_3; RegAddr[4:0] = out_5; RegData[31:0] = out_6; RegWrite = out_4; rst = reset

  // Notes on the sheet:
  //   contents of rom_1 (hex, n*v repeats v):
  //   8c120684 0 1b09020 0 ac100310 ac0d0560 20a3020 63a822 313022 8c0b04f8 ac010420 3c1576c6 ac1703d8
  //   3c1122fd 8c1506e0 0 ac190630 0 1b30820 8c120740 8c020784 2a95822 3570eeaa 8c180180 37359332 8c0a016c
  //   8c0803a0 ac0600d0 3c10414f 368408e3 0 8c0e04e8 255a022 1732822 2c83020 0 2779020 344a0a83 ac020290
  //   344947a3 c2a822 3c02025a 1433020
  //   SrcB
  //   WriteData
  //   Result
endmodule

module PC (
  input  [31:0] PC,
  input  clk,
  input  clr,
  output [31:0] PC_prime
);

  wire [31:0] register_1_q, subtractor_1_out;

  Subtractor #(.width(32)) subtractor_1 (.a(PC), .b(32'h3000), .out(subtractor_1_out));  // open: bin, bout
  Register #(.width(32)) register_1 (.D(subtractor_1_out), .Q(register_1_q), .clk(clk), .clr(clr));  // open: en
  Adder #(.width(32)) adder_1 (.a(register_1_q), .b(32'h3000), .out(PC_prime));  // open: cin, cout
endmodule

module IM (
  input  [31:0] PC,
  output [31:0] Instr
);

  wire [31:0] subtractor_1_out;

  Subtractor #(.width(32)) subtractor_1 (.a(PC), .b(32'h3000), .out(subtractor_1_out));  // open: bin, bout
  ROM #(.addrWidth(12), .dataWidth(32)) rom_1 (.addr(subtractor_1_out[13:2]), .data(Instr));  // open: sel

  // Notes on the sheet:
  //   contents of rom_1 (hex, n*v repeats v):
  //   8c120684 0 1b09020 0 ac100310 ac0d0560 20a3020 63a822 313022 8c0b04f8 ac010420 3c1576c6 ac1703d8
  //   3c1122fd 8c1506e0 0 ac190630 0 1b30820 8c120740 8c020784 2a95822 3570eeaa 8c180180 37359332 8c0a016c
  //   8c0803a0 ac0600d0 3c10414f 368408e3 0 8c0e04e8 255a022 1732822 2c83020 0 2779020 344a0a83 ac020290
  //   344947a3 c2a822 3c02025a 1433020
endmodule

module DM (
  input  [31:0] A,
  input  [31:0] WD,
  input  clk,
  input  WE,
  input  clr,
  output [31:0] RD
);

  wire not_1_out;

  RAM #(.addrWidth(12), .dataWidth(32), .bus("separate")) ram_1 (
    .addr(A[13:2]), .din(WD), .data(RD), .str(WE), .sel(1'b1), .clk(clk), .ld(not_1_out), .clr(clr));
  not not_1 (not_1_out, WE);
endmodule

module GRF (
  input  [31:0] WD3,
  input  [4:0] A2,
  input  [4:0] A3,
  input  WE3,
  input  rst,
  input  clk,
  input  [4:0] A1,
  output [31:0] RD2,
  output [31:0] RD1
);

  wire [31:0] i0, i1, i2, i3, i4, i5, i6, i7, i8, i9, i10, i11, i12, i13, i14, i15, i16, i17, i18, i19, i20,
       i21, i22, i23, i24, i25, i26, i27, i28, i29, i30, i31, o0, o1, o2, o3, o4, o5, o6, o7, o8, o9, o10,
       o11, o12, o13, o14, o15, o16, o17, o18, o19, o20, o21, o22, o23, o24, o25, o26, o27, o28, o29, o30,
       o31;

  Register #(.width(32)) _00 (.D({32{1'b0}}), .en(WE3), .Q(o0), .clk(clk), .clr(rst));
  Register #(.width(32)) _04 (.D(i4), .en(WE3), .Q(o4), .clk(clk), .clr(rst));
  Register #(.width(32)) _08 (.D(i8), .en(WE3), .Q(o8), .clk(clk), .clr(rst));
  Register #(.width(32)) _12 (.D(i12), .en(WE3), .Q(o12), .clk(clk), .clr(rst));
  Register #(.width(32)) _16 (.D(i16), .en(WE3), .Q(o16), .clk(clk), .clr(rst));
  Register #(.width(32)) _20 (.D(i20), .en(WE3), .Q(o20), .clk(clk), .clr(rst));
  Register #(.width(32)) _24 (.D(i24), .en(WE3), .Q(o24), .clk(clk), .clr(rst));
  Register #(.width(32)) _28 (.D(i28), .en(WE3), .Q(o28), .clk(clk), .clr(rst));
  Register #(.width(32)) _01 (.D(i1), .en(WE3), .Q(o1), .clk(clk), .clr(rst));
  Register #(.width(32)) _05 (.D(i5), .en(WE3), .Q(o5), .clk(clk), .clr(rst));
  Register #(.width(32)) _09 (.D(i9), .en(WE3), .Q(o9), .clk(clk), .clr(rst));
  Register #(.width(32)) _13 (.D(i13), .en(WE3), .Q(o13), .clk(clk), .clr(rst));
  Register #(.width(32)) _17 (.D(i17), .en(WE3), .Q(o17), .clk(clk), .clr(rst));
  Register #(.width(32)) _21 (.D(i21), .en(WE3), .Q(o21), .clk(clk), .clr(rst));
  Register #(.width(32)) _25 (.D(i25), .en(WE3), .Q(o25), .clk(clk), .clr(rst));
  Register #(.width(32)) _29 (.D(i29), .en(WE3), .Q(o29), .clk(clk), .clr(rst));
  Register #(.width(32)) _02 (.D(i2), .en(WE3), .Q(o2), .clk(clk), .clr(rst));
  Register #(.width(32)) _06 (.D(i6), .en(WE3), .Q(o6), .clk(clk), .clr(rst));
  Register #(.width(32)) _10 (.D(i10), .en(WE3), .Q(o10), .clk(clk), .clr(rst));
  Register #(.width(32)) _14 (.D(i14), .en(WE3), .Q(o14), .clk(clk), .clr(rst));
  Register #(.width(32)) _18 (.D(i18), .en(WE3), .Q(o18), .clk(clk), .clr(rst));
  Register #(.width(32)) _22 (.D(i22), .en(WE3), .Q(o22), .clk(clk), .clr(rst));
  Register #(.width(32)) _26 (.D(i26), .en(WE3), .Q(o26), .clk(clk), .clr(rst));
  Register #(.width(32)) _30 (.D(i30), .en(WE3), .Q(o30), .clk(clk), .clr(rst));
  Register #(.width(32)) _03 (.D(i3), .en(WE3), .Q(o3), .clk(clk), .clr(rst));
  Register #(.width(32)) _07 (.D(i7), .en(WE3), .Q(o7), .clk(clk), .clr(rst));
  Register #(.width(32)) _11 (.D(i11), .en(WE3), .Q(o11), .clk(clk), .clr(rst));
  Register #(.width(32)) _15 (.D(i15), .en(WE3), .Q(o15), .clk(clk), .clr(rst));
  Register #(.width(32)) _19 (.D(i19), .en(WE3), .Q(o19), .clk(clk), .clr(rst));
  Register #(.width(32)) _23 (.D(i23), .en(WE3), .Q(o23), .clk(clk), .clr(rst));
  Register #(.width(32)) _27 (.D(i27), .en(WE3), .Q(o27), .clk(clk), .clr(rst));
  Register #(.width(32)) _31 (.D(i31), .en(WE3), .Q(o31), .clk(clk), .clr(rst));
  Multiplexer #(.select(5), .width(32), .enable("false")) multiplexer_1 (
    .in0(o0), .in1(o1), .in2(o2), .in3(o3), .in4(o4), .in5(o5), .in6(o6), .in7(o7), .in8(o8), .in9(o9),
    .in10(o10), .in11(o11), .in12(o12), .in13(o13), .in14(o14), .in15(o15), .in16(o16), .in17(o17),
    .in18(o18), .in19(o19), .in20(o20), .in21(o21), .in22(o22), .in23(o23), .in24(o24), .in25(o25),
    .in26(o26), .in27(o27), .in28(o28), .in29(o29), .in30(o30), .in31(o31), .out(RD1), .sel(A1));
  Demultiplexer #(.select(5), .width(32), .tristate("true"), .enable("false")) demultiplexer_1 (
    .out0(i0), .out1(i1), .out2(i2), .out3(i3), .out4(i4), .out5(i5), .out6(i6), .out7(i7), .out8(i8),
    .out9(i9), .out10(i10), .out11(i11), .out12(i12), .out13(i13), .out14(i14), .out15(i15), .out16(i16),
    .out17(i17), .out18(i18), .out19(i19), .out20(i20), .out21(i21), .out22(i22), .out23(i23), .out24(i24),
    .out25(i25), .out26(i26), .out27(i27), .out28(i28), .out29(i29), .out30(i30), .out31(i31), .in(WD3),
    .sel(A3));
  Multiplexer #(.select(5), .width(32), .enable("false")) multiplexer_2 (
    .in0(o0), .in1(o1), .in2(o2), .in3(o3), .in4(o4), .in5(o5), .in6(o6), .in7(o7), .in8(o8), .in9(o9),
    .in10(o10), .in11(o11), .in12(o12), .in13(o13), .in14(o14), .in15(o15), .in16(o16), .in17(o17),
    .in18(o18), .in19(o19), .in20(o20), .in21(o21), .in22(o22), .in23(o23), .in24(o24), .in25(o25),
    .in26(o26), .in27(o27), .in28(o28), .in29(o29), .in30(o30), .in31(o31), .out(RD2), .sel(A2));
endmodule

module ALU (
  input  [3:0] ALUControl,
  input  [31:0] SrcA,
  input  [31:0] SrcB,
  output [31:0] ALUResult,
  output Zero
);

  wire and_3_out, and_4_out, and_5_out, comparator_1_lt, comparator_2_eq, comparator_3_eq, comparator_4_eq,
       comparator_5_eq, comparator_6_eq, comparator_7_eq, comparator_8_eq, comparator_9_eq,
       multiplexer_2_out, senodb;
  wire [5:0] behlbal, bitadder_1_out, bitadder_2_out;
  wire [5:1] bitadder_3_out;
  wire [31:0] add, \and , lui, multiplier_1_out, multiplier_2_out, \or , qaq, sll, sllv, slt, sub, \xor ,
       xor_2_out;

  Adder #(.width(32)) adder_1 (.a(SrcA), .b(SrcB), .out(add));  // open: cin, cout
  Subtractor #(.width(32)) subtractor_1 (.a(SrcA), .b(SrcB), .out(sub));  // open: bin, bout
  Comparator #(.width(32)) comparator_1 (.a(SrcA), .b(SrcB), .lt(comparator_1_lt));  // open: gt, eq
  assign \and  = SrcA & SrcB;  // AND_Gate and_1, 32 bits wide
  assign \or  = SrcA | SrcB;  // OR_Gate or_1, 32 bits wide
  BitAdder #(.width(32)) bitadder_1 (.in0(SrcA), .out(bitadder_1_out));
  BitAdder #(.width(32)) bitadder_2 (.in0(SrcB), .out(bitadder_2_out));
  assign slt = {{31{1'b0}}, comparator_1_lt};  // Bit_Extender bit_extender_1
  assign \xor  = SrcA ^ SrcB;  // XOR_Gate xor_1, 32 bits wide
  Shifter #(.width(32)) shifter_1 (.in(SrcB), .\dist (5'b10000), .out(lui));
  Multiplier #(.width(32)) multiplier_1 (.a(SrcA), .b(SrcA), .out(multiplier_1_out));  // open: cin, cout
  Multiplier #(.width(32)) multiplier_2 (.a(SrcB), .b(SrcB), .out(multiplier_2_out));  // open: cin, cout
  assign xor_2_out = SrcA ^ SrcB;  // XOR_Gate xor_2, 32 bits wide
  Shifter #(.width(32)) shifter_2 (.in(SrcB), .\dist (SrcA[4:0]), .out(sllv));
  Shifter #(.width(32)) shifter_3 (.in(SrcB), .\dist (SrcA[10:6]), .out(sll));
  Subtractor #(.width(6)) subtractor_2 (.a(bitadder_1_out), .b(bitadder_2_out), .out(behlbal));  // open: bin, bout
  assign qaq = multiplier_1_out & multiplier_2_out;  // AND_Gate and_2, 32 bits wide
  BitAdder #(.width(32)) bitadder_3 (.in0(xor_2_out), .out({bitadder_3_out, senodb}));
  Comparator #(.width(4)) comparator_2 (.a(ALUControl), .b(4'b0101), .eq(comparator_2_eq));  // open: gt, lt
  Comparator #(.width(6)) comparator_3 (.a(behlbal), .b({6{1'b0}}), .eq(comparator_3_eq));  // open: gt, lt
  Comparator #(.width(32)) comparator_4 (.a(sub), .b({32{1'b0}}), .eq(comparator_4_eq));  // open: gt, lt
  Comparator #(.width(4)) comparator_5 (.a(ALUControl), .b(4'b0110), .eq(comparator_5_eq));  // open: gt, lt
  Comparator #(.width(4)) comparator_6 (.a(ALUControl), .b(4'b0110), .eq(comparator_6_eq));  // open: gt, lt
  and and_3 (and_3_out, comparator_2_eq, comparator_3_eq);
  and and_4 (and_4_out, comparator_4_eq, comparator_5_eq);
  Comparator #(.width(1)) comparator_7 (.a(senodb), .b(1'b0), .eq(comparator_7_eq));  // open: gt, lt
  Comparator #(.width(4)) comparator_8 (.a(ALUControl), .b(4'b1001), .eq(comparator_8_eq));  // open: gt, lt
  Multiplexer #(.select(4), .width(32), .enable("false")) multiplexer_1 (
    .in0(\and ), .in1(\or ), .in2(add), .in3(lui), .in4(\xor ), .in6(sub), .in7(slt), .in8(qaq), .in10(sll),
    .in11(sllv), .out(ALUResult), .sel(ALUControl));  // open: in5, in9, in12, in13, in14, in15
  Comparator #(.width(4)) comparator_9 (.a(ALUControl), .b(4'b1001), .eq(comparator_9_eq));  // open: gt, lt
  Multiplexer #(.enable("false")) multiplexer_2 (
    .in0(and_3_out), .in1(and_4_out), .out(multiplexer_2_out), .sel(comparator_6_eq));
  Multiplexer #(.enable("false")) multiplexer_3 (
    .in0(multiplexer_2_out), .in1(and_5_out), .out(Zero), .sel(comparator_9_eq));
  and and_5 (and_5_out, comparator_7_eq, comparator_8_eq);

  // Notes on the sheet:
  //   s
  //   100
  //   000
  //   001
  //   010
  //   011
  //   110
  //   111
  //   1000
  //   1010
  //   1011
endmodule

module SPT (
  input  [31:0] in,
  output [15:0] _0_15,
  output [4:0] _16_20,
  output [4:0] _21_25,
  output [4:0] _11_15
);


  assign _0_15 = in[15:0];
  assign _11_15 = in[15:11];
  assign _16_20 = in[20:16];
  assign _21_25 = in[25:21];
endmodule

module EXT (
  input  [15:0] _15_0,
  input  ExtControl,
  output [31:0] SignImm
);

  wire [31:0] bit_extender_1_out, bit_extender_2_out;

  assign bit_extender_1_out = {{16{_15_0[15]}}, _15_0};  // Bit_Extender bit_extender_1
  assign bit_extender_2_out = {{16{1'b0}}, _15_0};  // Bit_Extender bit_extender_2
  Multiplexer #(.width(32), .enable("false")) multiplexer_1 (
    .in0(bit_extender_1_out), .in1(bit_extender_2_out), .out(SignImm), .sel(ExtControl));
endmodule

module NXTAD (
  input  Branch,
  input  [31:0] Instr,
  input  Jump,
  input  jr,
  input  Zero,
  input  [31:0] PC,
  input  [15:0] Imm,
  input  [31:0] GPR_rs,
  output [31:0] PC_prime,
  output [31:0] PC_4
);

  wire and_1_out;
  wire [31:0] beq, bit_extender_1_out, multiplexer_1_out, multiplexer_2_out, shifter_1_out;

  assign bit_extender_1_out = {{16{Imm[15]}}, Imm};  // Bit_Extender bit_extender_1
  Adder #(.width(32)) adder_1 (.a(PC), .b(32'h4), .out(PC_4));  // open: cin, cout
  Shifter #(.width(32)) shifter_1 (.in(bit_extender_1_out), .\dist (5'b00010), .out(shifter_1_out));
  Adder #(.width(32)) adder_2 (.a(shifter_1_out), .b(PC_4), .out(beq));  // open: cin, cout
  and and_1 (and_1_out, Branch, Zero);
  Multiplexer #(.width(32), .enable("false")) multiplexer_1 (
    .in0(PC_4), .in1(beq), .out(multiplexer_1_out), .sel(and_1_out));
  Multiplexer #(.width(32), .enable("false")) multiplexer_2 (
    .in0(multiplexer_1_out), .in1({PC_4[31:28], Instr[25:0], 2'b00}), .out(multiplexer_2_out), .sel(Jump));
  Multiplexer #(.width(32), .enable("false")) multiplexer_3 (
    .in0(multiplexer_2_out), .in1(GPR_rs), .out(PC_prime), .sel(jr));
endmodule

module CU (
  input  in_1,
  input  [31:0] in,
  output RegWrite,
  output MemWrite,
  output [3:0] ALUControl,
  output ALUSrc,
  output MemtoReg,
  output RegDst,
  output Branch,
  output Jump,
  output ExtControl,
  output behlbal,
  output senodb,
  output ALUSrcA,
  output jr,
  output jal
);

  wire add, addi, \and , and_12_out, behlbal_t, beq, blez, comparator_1_eq, comparator_2_eq, comparator_3_eq,
       comparator_4_eq, comparator_5_eq, comparator_6_eq, comparator_7_eq, comparator_8_eq, comparator_9_eq,
       comparator_10_eq, comparator_11_eq, j, jal_t, jr_t, lui, lw, \or , ori, pull_resistor_1_node, qaq,
       \R型指令 , \R指令_2_out , \R指令_out , senodb_t, sll, sllv, slt, slti, sub, sw, \xor ;

  Comparator #(.width(6), .mode("unsigned")) comparator_1 (
    .a(in[5:0]), .b(6'b100000), .eq(comparator_1_eq));  // open: gt, lt
  Comparator #(.width(6)) comparator_2 (.a(in[5:0]), .b(6'b100010), .eq(comparator_2_eq));  // open: gt, lt
  Comparator #(.width(6)) comparator_3 (.a(in[5:0]), .b(6'b100100), .eq(comparator_3_eq));  // open: gt, lt
  Comparator #(.width(6)) comparator_4 (.a(in[5:0]), .b(6'b100101), .eq(comparator_4_eq));  // open: gt, lt
  Comparator #(.width(6)) comparator_5 (.a(in[5:0]), .b(6'b101010), .eq(comparator_5_eq));  // open: gt, lt
  Comparator #(.width(6)) comparator_6 (.a(in[5:0]), .b(6'b100110), .eq(comparator_6_eq));  // open: gt, lt
  Comparator #(.width(6)) comparator_7 (.a(in[5:0]), .b(6'b010110), .eq(comparator_7_eq));  // open: gt, lt
  Comparator #(.width(6)) comparator_8 (.a(in[5:0]), .b(6'b001111), .eq(comparator_8_eq));  // open: gt, lt
  Comparator #(.width(6)) comparator_9 (.a(in[5:0]), .b(6'b000100), .eq(comparator_9_eq));  // open: gt, lt
  Comparator #(.width(6)) comparator_10 (.a(in[5:0]), .b({6{1'b0}}), .eq(comparator_10_eq));  // open: gt, lt
  Comparator #(.width(6)) comparator_11 (.a(in[5:0]), .b(6'b001000), .eq(comparator_11_eq));  // open: gt, lt
  Comparator #(.width(6)) comparator_12 (.a(in[31:26]), .b(6'b100011), .eq(lw));  // open: gt, lt
  Comparator #(.width(6)) comparator_13 (.a(in[31:26]), .b(6'b101011), .eq(sw));  // open: gt, lt
  Comparator #(.width(6)) comparator_14 (.a(in[31:26]), .b(6'b000100), .eq(beq));  // open: gt, lt
  Comparator #(.width(6)) comparator_15 (.a(in[31:26]), .b({6{1'b0}}), .eq(\R型指令 ));  // open: gt, lt
  Comparator #(.width(6)) comparator_16 (.a(in[31:26]), .b(6'b001000), .eq(addi));  // open: gt, lt
  Comparator #(.width(6)) comparator_17 (.a(in[31:26]), .b(6'b000010), .eq(j));  // open: gt, lt
  Comparator #(.width(6)) comparator_18 (.a(in[31:26]), .b(6'b001101), .eq(ori));  // open: gt, lt
  Comparator #(.width(6)) comparator_19 (.a(in[31:26]), .b(6'b001111), .eq(lui));  // open: gt, lt
  Comparator #(.width(6)) comparator_20 (.a(in[31:26]), .b(6'b111110), .eq(behlbal_t));  // open: gt, lt
  Comparator #(.width(6)) comparator_21 (.a(in[31:26]), .b(6'b000011), .eq(jal_t));  // open: gt, lt
  Comparator #(.width(6)) comparator_22 (.a(in[31:26]), .b(6'b001010), .eq(slti));  // open: gt, lt
  Comparator #(.width(6)) comparator_23 (.a(in[31:26]), .b(6'b000110), .eq(blez));  // open: gt, lt
  and and_1 (add, comparator_1_eq, \R型指令 );
  and and_2 (sub, comparator_2_eq, \R型指令 );
  and and_3 (\and , comparator_3_eq, \R型指令 );
  and and_4 (\or , comparator_4_eq, \R型指令 );
  and and_5 (slt, comparator_5_eq, \R型指令 );
  and and_6 (\xor , comparator_6_eq, \R型指令 );
  and and_7 (qaq, comparator_7_eq, \R型指令 );
  and and_8 (senodb_t, comparator_8_eq, \R型指令 );
  and and_9 (sllv, comparator_9_eq, \R型指令 );
  and and_10 (sll, comparator_10_eq, \R型指令 );
  and and_11 (jr_t, comparator_11_eq, \R型指令 );
  or \R指令  (\R指令_out , sllv, senodb_t, add, sub, \and , \or , slt, \xor , qaq, sll);
  and and_12 (and_12_out, in_1, behlbal_t);
  or \R指令_2  (\R指令_2_out , sllv, qaq, add, sub, \and , \or , slt, \xor , senodb_t, sll);
  Pull_Resistor pull_resistor_1 (.node(pull_resistor_1_node));
  or or_1 (MemWrite, pull_resistor_1_node, sw);
  or _0 (ALUControl[0], senodb_t, lui, pull_resistor_1_node, slt, ori, \or , behlbal_t, sllv, slti);
  or _1 (ALUControl[1], blez, sub, beq, slt, pull_resistor_1_node, lui, add, lw, sw, sllv, sll, slti);
  or _2 (ALUControl[2], blez, slt, pull_resistor_1_node, sub, beq, \xor , behlbal_t, slti);
  or _3 (ALUControl[3], pull_resistor_1_node, qaq, senodb_t, sllv, sll);
  or or_2 (ALUSrc, lui, addi, pull_resistor_1_node, lw, sw, ori, slti);
  or or_3 (MemtoReg, pull_resistor_1_node, lw);
  or or_4 (RegDst, pull_resistor_1_node, \R指令_2_out );
  or or_5 (Branch, pull_resistor_1_node, blez, behlbal_t, beq);
  or or_6 (Jump, pull_resistor_1_node, jal_t, j);
  or or_7 (ExtControl, pull_resistor_1_node, ori, lui);
  or or_8 (RegWrite, and_12_out, lui, \R指令_out , pull_resistor_1_node, addi, lw, ori, jal_t, slti);
  or or_9 (behlbal, behlbal_t, pull_resistor_1_node);
  or or_10 (senodb, pull_resistor_1_node, senodb_t);
  or or_11 (ALUSrcA, pull_resistor_1_node, sll);
  or or_12 (jr, pull_resistor_1_node, jr_t);
  or or_13 (jal, pull_resistor_1_node, jal_t);

  // Other names for the same wires on the sheet: Funct[5:0] = in[5:0]; Op[5:0] = in[31:26]; zero = in_1

  // Notes on the sheet:
  //   lw
  //   sw
  //   beq
  //   addi
  //   j
  //   ori
  //   lui
  //   lui
  //   jal
  //   jal
  //   blez
  //   1001
  //   011
  //   111
  //   001
  //   001
  //   101
  //   1011
  //   111
  //   110
  //   110
  //   110
  //   111
  //   011
  //   010
  //   010
  //   010
  //   1011
  //   1010
  //   111
  //   110
  //   111
  //   110
  //   110
  //   100
  //   101
  //   111
  //   1000
  //   1001
  //   1011
  //   1010
  //   111
endmodule
