// Logisim project cpu_test.circ as structural Verilog: 2 circuits, main circuit main
module main (
  output [31:0] out_1,
  output [31:0] out_2,
  output out_3,
  output [4:0] out_4,
  output [31:0] out_5,
  output halt,
  output out_7,
  output [31:0] out_8,
  output [31:0] out_9
);

  wire clock_1_out, comparator_1_gt;
  wire [7:0] counter_1_q;

  Clock clock_1 (.out(clock_1_out));
  Counter #(.ongoal("stay")) counter_1 (.Q(counter_1_q), .carry(halt), .clk(clock_1_out));  // open: load, D, count, clr
  Comparator #(.mode("unsigned")) comparator_1 (.a(8'h4), .b(counter_1_q), .gt(comparator_1_gt));  // open: eq, lt
  cpu_main main_1 (
    .reset(comparator_1_gt), .out_2(out_1), .out_3(out_2), .out_4(out_3), .out_5(out_4), .out_6(out_5),
    .out_7(out_7), .out_8(out_8), .out_9(out_9));
endmodule

module student (
  input  in_1,
  output [31:0] out_2,
  output [31:0] out_3,
  output out_4,
  output [4:0] out_5,
  output [31:0] out_6,
  output out_7,
  output [31:0] out_8,
  output [31:0] out_9
);
endmodule
